# Fritzing sketch Coche Fritzing (saved by Fritzing 0.9.2b)
breadboards: 2

parts:
  Part1 = Arduino Uno (Rev3)
  Part3 = SRF05 Ultrasonic Rangefinder
  Part4 = Bluetooth HC-05 Macho
  LED1 = smd LED [color="Red (633nm)" package="0805 [SMD]"]
  R1 = Resistor [tolerance=±5% resistance=220 package=THT]
  LED2 = smd LED [color="Red (633nm)" package="0805 [SMD]"]
  R2 = Resistor [tolerance=±5% resistance=220 package=THT]

nets:
  N1: Part1.D9_PWM, R1.Pin_0
  N2: Part1.D10_PWM/SS, R2.Pin_1
  N3: Part1.D12/MISO, Part3.Trig
  N4: Part1.D13/SCK, Part3.Echo
  N5: Part1.D2, Part4.TXD
  N6: Part1.D3_PWM, Part4.RXD
  VCC: Part1.5V, Part3.VCC, Part4.VCC, LED2.cathode
  GND: Part1.GND, Part3.GND, Part4.GND, LED1.anode
  N7: LED1.cathode, R1.Pin_1
